# Fritzing sketch schema (saved by Fritzing 0.9.3b)
stripboards: 1

parts:
  Part2 = Bluetooth HC-05 Macho
  Part3 = NRF24L01
  Laser_LED = LED - 3mm [color="Red (660nm)" current=0.030 package="3 mm [THT]"]
  Part4 = Arduino Uno (Rev3) - ICSP
  R6 = Resistor [tolerance=±5% power=0.25 resistance=7.5k package=THT]
  R7 = Resistor [tolerance=±5% power=0.25 resistance=7.5k package=THT]
  R8 = Resistor [tolerance=±5% power=0.25 resistance=7.5k package=THT]
  Q1 = LTR-301 [package=ltr-301]
  R9 = Resistor [tolerance=±5% power=0.25 resistance=10k package=THT]
  C2 = Electrolytic Capacitor [capacitance=10µF package="200 mil [THT, electrolytic]"]
  S1 = Round Pushbutton
  R10 = Resistor [tolerance=±5% resistance=10k package=THT]

nets:
  N1: Part2.TXD, Part4.D0/RX
  N2: Part2.RXD, R7.Pin_1, R8.Pin_0
  VCC: Part2.VCC, Part4.5V, Q1.C, S1.leg0
  GND: Part2.GND, Part3.GND, Laser_LED.cathode, Part4.GND, R6.Pin_0, R9.Pin_0, C2.-, R10.Pin_1
  N3: Part3.MOSI, Part4.D11_PWM/MOSI
  N4: Part3.CSN, Part4.D8
  VCC_2: Part3.VCC, Part4.3V3, C2.+
  N5: Part3.MISO, Part4.ICSP_MISO, Part4.D12/MISO
  N6: Part3.SCK, Part4.D13/SCK
  N7: Part3.CE, Part4.D7
  N8: Laser_LED.anode, Part4.D3_PWM
  N9: Part4.A5/SCL, Q1.E, R9.Pin_1
  N10: Part4.D9_PWM, S1.leg1, R10.Pin_0
  N11: Part4.D1/TX, R8.Pin_1
  N12: R6.Pin_1, R7.Pin_0
